# Fritzing sketch Doorbell (saved by Fritzing 1.0.6)

parts:
  Cam_Online_led = LEDs [package=led10mm]
  Microphone_(Built-in_to_sense) = MIC [package=mic_electret_smd]  # not connected
  Doorbell_Button = Round Pushbutton
  Call_Button = Round Pushbutton
  Ready_LED = LEDs [package=led10mm]
  WARN_led = LEDs [package=led10mm]
  LCD_Screen = 1_54in tft lcd
  NFC_PN532 = PN532 Elechouse RFID NFC Module V3
  Amp_module = ESP32-S3-DevKitC-1-N8R8-v1 [part_number=ESP32-S3-DevKitC-1-N8R8-v1]
  AMP = Stereo 3.7W Class D Amplifier [mn="Maxim Integrated" mpn=MAX98357BETE+ package=16-TQFN]
  Speaker = SPEAKER [package=pcb_mount_speaker]
  R1 = Resistor [tolerance=±5% resistance=220 package="2512 [SMD]"]
  Speaker_LED = LEDs [package=led10mm]
  Power_LED = LEDs [package=led10mm]
  ESP32S1 = XIAO ESP32S3(SENCE) [chip_label=ESP32S3(sense)]
  A1 = ESP32 DOIT DEVKIT V1 36pin

nets:
  N1: Cam_Online_led.C, Ready_LED.C, WARN_led.C, LCD_Screen.pin_1, Amp_module.pin_22, Amp_module.pin_24, Amp_module.pin_44, AMP.GND#2, AMP.SD_MODE, R1.Pin_1, Speaker_LED.C, Power_LED.C, ESP32S1.GND, A1.Pin_17
  N2: Cam_Online_led.A, ESP32S1.D1
  N3: Doorbell_Button.leg0, Call_Button.leg0, Power_LED.A, A1.Pin_19
  N4: Doorbell_Button.leg1, A1.Pin_5
  N5: Call_Button.leg1, A1.Pin_4
  N6: Ready_LED.A, A1.Pin_25
  N7: WARN_led.A, A1.Pin_26
  N8: LCD_Screen.pin2, LCD_Screen.pin_8, Amp_module.pin_21, A1.Pin_18
  N9: LCD_Screen.pin3, A1.Pin_35
  N10: LCD_Screen.pin4, A1.Pin_36
  N11: LCD_Screen.pin_5, A1.Pin_30
  N12: LCD_Screen.pin_6, A1.Pin_31
  N13: LCD_Screen.pin_7, A1.Pin_32
  N14: NFC_PN532.SDA, A1.Pin_13
  N15: NFC_PN532.SCL, A1.Pin_24
  N16: NFC_PN532.IRQ, A1.Pin_29
  N17: Amp_module.pin_6, Speaker_LED.A
  N18: Amp_module.pin_7, AMP.LRCLK
  N19: Amp_module.pin_12, AMP.BCLK
  N20: Amp_module.pin_15, AMP.DIN
  N21: AMP.GAIN__SLOT, R1.Pin_0
  N22: AMP.OUTP, Speaker.+
  N23: AMP.GND#10, Speaker.-
  N24: ESP32S1.D2, A1.Pin_11
  N25: ESP32S1.D5, A1.Pin_27
  N26: ESP32S1.D6, A1.Pin_28
  N27: ESP32S1.D7, A1.Pin_8
  N28: ESP32S1.D8, A1.Pin_9
  N29: ESP32S1.D9, A1.Pin_10

custom parts:
  1_54in tft lcd: This is the DONGKER 1.54'' LCD Display Module, SPI 240x240 1.54'' LCD Display Module ST7789 Driver 240x240 3.3V IPS LCD Display Screen Module. The 1.54" display has 240x240 color pixels.
  PN532 Elechouse RFID NFC Module V3: NFC is a popular technology in recent years. We often heard this work while smart phone company such as Samsung or HTC introduces their latest high-end phones. Almost all the high-end phone in the market support NFC. Near field communication (NFC) is a set of standards for smart phones and similar devices to establish radio communication with each other by touching them together or bringing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
  ESP32-S3-DevKitC-1-N8R8-v1: ESP32-S3-DevKitC-1-N8R8-v1 This module is 44pins long (2x22) and 11 pins width.
  Stereo 3.7W Class D Amplifier: Mono 3.2W Class D Amplifier Datasheet: https://datasheets.maximintegrated.com/en/ds/MAX98357A-MAX98357B.pdf The MAX98357B is an easy-to-use, low-cost, digital pulse-code modulation (PCM) input Class D amplifier that provides industry-leading Class AB audio performance with Class D efficiency. The digital audio interface automatically recognizes up to 35 different PCM and TDM clocking schemes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
  XIAO ESP32S3(SENCE): Seeed Studio XIAO ESP32S3 leverages dual-core ESP32S3 chip, supporting both Wi-Fi and BLE wireless connectivities, which allows battery charge. It integrates built-in camera sensor, digital microphone. It offers 8MB PSRAM, 8MB FLASH, and external SD card slot. All of these make it suitable for embedded ML, like intelligent voice and vision AI.
  ESP32 DOIT DEVKIT V1 36pin: ESP32 DOIT DEVKIT V1 36pin.
