# Fritzing sketch Danny's & Valentina-SmartAirPurifierFritzing PCB (saved by Fritzing 1.0.2b)
circuit board: 16cm x 11.6cm
breadboards: 1

parts:
  HC-06 = Bluetooth HC-06u [package=THT]
  AHT20 = Adafruit AHT20 Temperature and Humidity Sensor [part_number="Adafruit #4566"]
  SGP40 = Adafruit SGP40
  FAN = Fan - Ventilador [package=THT]
  Arduino = Arduino Uno (Rev3) - ICSP
  Push_button = Momentary Switch [package=ksa_sealed_tac_switch]
  PM2_5_Air_Quality_Sensor = PMS5003
  U2 = Nokia 6100 Color LCD [package=nokia6100_lcd]
  L298N = L298N DC motor driver
  JACK1 = 2.1mm Barrel Jack with Terminal Block

nets (from the pcb view):
  VCC: HC-06.VCC, AHT20.VCC, SGP40.VCC, Arduino.5V, PM2_5_Air_Quality_Sensor.VCC, U2.5V
  GND: HC-06.GND, AHT20.GND, SGP40.GND, Arduino.GND, Push_button.4, PM2_5_Air_Quality_Sensor.GND, U2.GND, JACK1.NEG
  N1: HC-06.TXD, Arduino.ICSP_MOSI, Arduino.D11_PWM/MOSI
  N2: HC-06.RXD, Arduino.D10_PWM/SS
  N3: AHT20.SCL, SGP40.SCL, Arduino.A5/SCL
  N4: AHT20.SDA, SGP40.SDA, Arduino.A4/SDA
  N5: FAN.5V, L298N.ENB
  N6: FAN.GND, L298N.IN3
  N7: Arduino.D8, L298N.IN2
  N8: Arduino.D0/RX, U2.RX
  N9: Arduino.D1/TX, U2.TX
  N10: Arduino.D2, Push_button.2
  N11: Arduino.D3_PWM, PM2_5_Air_Quality_Sensor.TX
  N12: Arduino.D4, PM2_5_Air_Quality_Sensor.RX
  N13: Arduino.D5_PWM, L298N.ENA
  N14: Arduino.D7, L298N.IN1
  N15: L298N.12V, L298N.5V-ENA-JMP-O

custom parts:
  Bluetooth HC-06u: Bluetooth HC-06 - face up, pins down 16.5mm x 37.5mm PCB
  Adafruit AHT20 Temperature and Humidity Sensor: The AHT20 is a nice but inexpensive temperature and humidity sensor from the same folks that brought us the DHT22. You can take sensor readings as often as you like, and it uses standard I2C so its super easy to use with any Arduino or Linux/Raspberry Pi board. This sensor has a typical accuracy of +- 2% relative humidity, and +-0.3 °C. There is only one I2C address so its not a good option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
  Fan - Ventilador: Ventilador de 2 pines, se encuentra comunmente en computadoras de escritorio
  PMS5003: PMS5003 is a kind of digital and universal particle concentration sensor, which can be used to obtain the number of suspended particles in the air.
  Nokia 6100 Color LCD: Nokia 6100 Color LCD Schematic element and footprint production proven but could use some touching up. Spark Fun Electronics SKU : LCD-00569. Mating SMD connector : LCD-00570
  L298N DC motor driver: 2x DC motor driver with 78M05 positive voltage regulator (7..35 V) L298N: max 46 V, 2 A Set 5 V Enable jumper to enable 5 V regultor (needed for the L298N) and +5 V output at screw terminal or supply external +5 V at screw terminal Set ENA and/or ENB to +5 V to enable motor permanently or supply ENA and/or ENB with PWM signal IN1 and IN2 set rotation directory for motor A (OUT1/OUT2) IN2 and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
