# Fritzing sketch Hub (saved by Fritzing 1.0.6)

parts:
  Main_ESP32_Wroover = ESP32 DOIT DEVKIT V1 36pin
  Mesh_Module = ESP32-S3-DevKitC-1-N8R8-v1 [part_number=ESP32-S3-DevKitC-1-N8R8-v1]
  Touch_Screen = Adafruit RA8875 Driver Board for 40-pin TFT Touch Displays [part_number="Adafruit #1590"]
  DHT11 = Humidity and Temperature Sensor DHT11
  AMP_Module = ESP32-S3-DevKitC-1-N8R8-v1 [part_number=ESP32-S3-DevKitC-1-N8R8-v1]
  PM_Sensor = PMS5003
  Amp = Stereo 3.7W Class D Amplifier [mn="Maxim Integrated" mpn=MAX98357BETE+ package=16-TQFN]
  R1 = Resistor [tolerance=±5% resistance=220 package="2512 [SMD]"]
  Speaker1 = SPEAKER [package=pcb_mount_speaker]
  Touch_pads = Adafruit MPR121 Gator
  Microphone = INMP441
  Rotary_Encoder = Rotary Encoder [package=THT]

nets:
  N1: Main_ESP32_Wroover.Pin_4, Touch_Screen.INT
  N2: Main_ESP32_Wroover.Pin_5, Rotary_Encoder.EncoderPinC
  N3: Main_ESP32_Wroover.Pin_6, Microphone.WS
  N4: Main_ESP32_Wroover.Pin_7, AMP_Module.pin_10
  N5: Main_ESP32_Wroover.Pin_8, Mesh_Module.pin_9
  N6: Main_ESP32_Wroover.Pin_9, Mesh_Module.pin_11
  N7: Main_ESP32_Wroover.Pin_10, Rotary_Encoder.EncoderPinB
  N8: Main_ESP32_Wroover.Pin_11, Rotary_Encoder.EncoderPinA
  N9: Main_ESP32_Wroover.Pin_12, Microphone.SCK
  N10: Main_ESP32_Wroover.Pin_13, Microphone.SD
  GND: Main_ESP32_Wroover.Pin_17, Mesh_Module.pin_22, Mesh_Module.pin_23, Mesh_Module.pin_44, Touch_Screen.GND, DHT11.GND, AMP_Module.pin_22, PM_Sensor.Pin_2, Amp.GND, Amp.SD_MODE, R1.Pin_1, Touch_pads.GND, Microphone.GND
  VIN: Main_ESP32_Wroover.Pin_18, Mesh_Module.pin_21, Touch_Screen.BACKLITE, Touch_Screen.VIN, Touch_pads.VCC
  N11: Main_ESP32_Wroover.Pin_19, Microphone.VDD
  N12: Main_ESP32_Wroover.Pin_26, AMP_Module.pin_11
  N13: Main_ESP32_Wroover.Pin_29, Touch_Screen.CS
  N14: Main_ESP32_Wroover.Pin_30, Touch_Screen.SCK
  N15: Main_ESP32_Wroover.Pin_31, Touch_Screen.MISO
  N16: Main_ESP32_Wroover.Pin_32, Touch_Screen.X-, Touch_pads.SDA
  N17: Main_ESP32_Wroover.Pin_35, Touch_Screen.Y+, Touch_pads.SCL
  N18: Main_ESP32_Wroover.Pin_36, Touch_Screen.MOSI
  N19: Mesh_Module.pin_1, Mesh_Module.pin_2, DHT11.Vcc
  N20: Mesh_Module.pin_4, DHT11.Data
  N21: Mesh_Module.pin_17, PM_Sensor.Pin_5
  N22: AMP_Module.pin_7, Amp.LRCLK
  N23: AMP_Module.pin_12, Amp.BCLK
  N24: AMP_Module.pin_15, Amp.DIN
  N25: AMP_Module.pin_21, PM_Sensor.Pin_1
  N26: Amp.GAIN__SLOT, R1.Pin_0
  N27: Amp.OUTP, Speaker1.+
  N28: Amp.OUTN, Speaker1.-

custom parts:
  ESP32 DOIT DEVKIT V1 36pin: ESP32 DOIT DEVKIT V1 36pin.
  ESP32-S3-DevKitC-1-N8R8-v1: ESP32-S3-DevKitC-1-N8R8-v1 This module is 44pins long (2x22) and 11 pins width.
  Adafruit RA8875 Driver Board for 40-pin TFT Touch Displays: Have you gazed longingly at large TFT displays - you know what I'm talking about here, 4", 5" or 7" TFTs with up to 800x480 pixels. Then you look at your Arduino. You love your Arduino (you really do!) but there's no way it can control a display like that, one that requires 60Hz refresh and 4 MHz pixel clocking. Heck, it doesn't even have enough pins. I suppose you could move to ARM core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
  Humidity and Temperature Sensor DHT11: Digital relative humidity & temperature sensor DHT11
  PMS5003: PMS5003 is a kind of digital and universal particle concentration sensor, which can be used to obtain the number of suspended particles in the air.
  Stereo 3.7W Class D Amplifier: Mono 3.2W Class D Amplifier Datasheet: https://datasheets.maximintegrated.com/en/ds/MAX98357A-MAX98357B.pdf The MAX98357B is an easy-to-use, low-cost, digital pulse-code modulation (PCM) input Class D amplifier that provides industry-leading Class AB audio performance with Class D efficiency. The digital audio interface automatically recognizes up to 35 different PCM and TDM clocking schemes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
  INMP441: This is a simple breakout board for the INMP441 I2S MEMS microphone.
