# Fritzing sketch Sensor (saved by Fritzing 1.0.6)

parts:
  MCU1 = Wemos Lolin32lite
  Gas_Sensor = Adafruit MiCS-5524 Gas Sensor [part_number="Adafruit #3199"]
  AHT25_(no_1_to_1_part) = Adafruit AHT20 Temperature and Humidity Sensor [part_number="Adafruit #4566"]
  VEML_Light = VEML7700 [part_number="Adafruit #4162"]
  A1 = mini boost module

nets:
  N1: MCU1.pin_4, Gas_Sensor.AOUT
  N2: MCU1.pin_8, Gas_Sensor.ENABLE
  GND: MCU1.pin_13, AHT25_(no_1_to_1_part).GND, VEML_Light.GND, A1.Pin_1
  N3: MCU1.pin_14, A1.Pin_2
  N4: MCU1.pin_26, AHT25_(no_1_to_1_part).SDA, VEML_Light.SDA
  N5: MCU1.pin_27, AHT25_(no_1_to_1_part).SCL, VEML_Light.SCL
  VCC: MCU1.pin_28, AHT25_(no_1_to_1_part).VCC, VEML_Light.3.3V
  N6: Gas_Sensor.5.0V, A1.Pin_4
  N7: Gas_Sensor.GND, A1.Pin_3

custom parts:
  Wemos Lolin32lite: Wemos Lolinlite32 wifi and blue tooth board based on the ESP-32 cpu, digital I/Os 19, analog inputs 6, clock 240mhz, Flash 4Mbytes, lipo battery charger (500ma connection broken out on breadboard but not pcb), usb.
  Adafruit MiCS-5524 Gas Sensor: Give your next sensor project a nose for gasses with the Adafruit MiCS-5524 Gas Sensor Breakout. This breakout makes it easy to use this nice sensor from SGX Sensortech. The MiCS-5524 is a robust MEMS sensor for indoor carbon monoxide and natural gas leakage detection, it's suitable also for indoor air quality monitoring; breath checker and early fire detection. Please note: This sensor is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
  Adafruit AHT20 Temperature and Humidity Sensor: The AHT20 is a nice but inexpensive temperature and humidity sensor from the same folks that brought us the DHT22. You can take sensor readings as often as you like, and it uses standard I2C so its super easy to use with any Arduino or Linux/Raspberry Pi board. This sensor has a typical accuracy of +- 2% relative humidity, and +-0.3 °C. There is only one I2C address so its not a good option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
  mini boost module: mini boost module.
